# Fritzing sketch Deksel (saved by Fritzing 0.9.5d)
perfboards: 2

parts:
  U1 = AVR 10-pin ICSP Header [package=2x5-shrouded_smd]
  LED1 = smd LED [color="Blue (470nm)" package="0603 [SMD]"]
  LED2 = smd LED [color="White (4500K)" package="0603 [SMD]"]
  S1 = Momentary Switch [package=ksa_sealed_tac_switch]
  R1 = Resistor [tolerance=±2% resistance=220 package=THT]
  R2 = Resistor [tolerance=±2% resistance=220 package=THT]
  U2 = AVR 10-pin ICSP Header [package=2x5-shrouded_smd]
  WeMos_D1_Mini_Relay_Shield1 = WeMos D1 Mini Relay Shield
  U3 = ESP8266 NodeMCU LoLin module

nets:
  N1: U1.2, R1.Pin_1
  N2: U1.4, R2.Pin_1
  N3: U1.6, S1.2
  N4: U1.10, LED1.cathode, LED2.cathode, S1.4
  N5: LED1.anode, R1.Pin_0
  N6: LED2.anode, R2.Pin_0
  N7: U2.2, U3.connector3
  N8: U2.4, U3.connector4
  N9: U2.6, U3.connector7
  N10: U2.10, WeMos_D1_Mini_Relay_Shield1.G, U3.connector16
  N11: WeMos_D1_Mini_Relay_Shield1.5V, U3.connector15
  N12: WeMos_D1_Mini_Relay_Shield1.A0, U3.connector8
