# Fritzing sketch tuin13 (saved by Fritzing 0.9.5d)
breadboards: 1

parts:
  MH-ET_LIVE_ESP32_DEVKIT1 = MH-ET LIVE ESP32 DEVKIT
  S1 = Momentary Switch [package=ksa_sealed_tac_switch]
  S2 = Momentary Switch [package=ksa_sealed_tac_switch]
  LED1 = LED - 3mm [color="Red (633nm)" package="3 mm [THT]"]
  LED2 = LED - 3mm [color="Red (633nm)" package="3 mm [THT]"]
  R1 = Resistor [tolerance=±5% resistance=470 package=THT]
  R2 = Resistor [tolerance=±5% resistance=470 package=THT]
  WeMos_D1_Mini_Relay_Shield_V1 = WeMos D1 Mini Relay Shield V2
  LED3 = LED - 3mm [color="Red (633nm)" package="3 mm [THT]"]

nets:
  N1: MH-ET_LIVE_ESP32_DEVKIT1.connector51, WeMos_D1_Mini_Relay_Shield_V1.A0
  N2: MH-ET_LIVE_ESP32_DEVKIT1.connector52, LED2.cathode
  N3: MH-ET_LIVE_ESP32_DEVKIT1.connector53, LED1.cathode
  N4: MH-ET_LIVE_ESP32_DEVKIT1.connector56, S2.4
  N5: MH-ET_LIVE_ESP32_DEVKIT1.connector58, S1.3, S2.3, R1.Pin_1, R2.Pin_1, WeMos_D1_Mini_Relay_Shield_V1.G, LED3.anode
  N6: MH-ET_LIVE_ESP32_DEVKIT1.connector59, S1.4
  N7: MH-ET_LIVE_ESP32_DEVKIT1.connector63, WeMos_D1_Mini_Relay_Shield_V1.3V3, WeMos_D1_Mini_Relay_Shield_V1.NC
  N8: LED1.anode, R2.Pin_0
  N9: LED2.anode, R1.Pin_0
  N10: WeMos_D1_Mini_Relay_Shield_V1.COM, LED3.cathode
